// Logisim project Additionneur complet.circ as structural Verilog
module Additionneur_complet (
  input  [3:0] in_1,
  input  [3:0] in_2
);

  wire adder_1_cout, adder_2_cout, adder_3_cout;
  wire [7:1] undriven, undriven_2, undriven_3, undriven_4, undriven_5, undriven_6, undriven_7, undriven_8;

  Adder adder_1 (.a({undriven, in_1[0]}), .b({undriven_5, in_2[0]}), .cout(adder_1_cout));  // open: out, cin
  Adder adder_2 (
    .a({undriven_2, in_1[1]}), .b({undriven_6, in_2[1]}), .cin(adder_1_cout), .cout(adder_2_cout));  // open: out
  Adder adder_3 (
    .a({undriven_3, in_1[2]}), .b({undriven_7, in_2[2]}), .cin(adder_2_cout), .cout(adder_3_cout));  // open: out
  Adder adder_4 (.a({undriven_4, in_1[3]}), .b({undriven_8, in_2[3]}), .cin(adder_3_cout));  // open: out, cout
  // Pins of 1 and 8 bits meet at {undriven_5, in_2[0]}
  // Pins of 1 and 8 bits meet at {undriven_6, in_2[1]}
  // Pins of 1 and 8 bits meet at {undriven_7, in_2[2]}
  // Pins of 1 and 8 bits meet at {undriven_8, in_2[3]}
  // Pins of 1 and 8 bits meet at {undriven, in_1[0]}
  // Pins of 1 and 8 bits meet at {undriven_3, in_1[2]}
  // Pins of 1 and 8 bits meet at {undriven_2, in_1[1]}
  // Pins of 1 and 8 bits meet at {undriven_4, in_1[3]}
endmodule
