// Logisim project Ou exclusif.circ as structural Verilog: 1 circuit, main circuit main
module main (
  input  a,
  input  b,
  output out_3
);

  wire and_1_out, and_2_out, not_1_out, not_2_out;

  and and_1 (and_1_out, a, not_1_out);
  not not_1 (not_1_out, b);
  not not_2 (not_2_out, a);
  and and_2 (and_2_out, not_2_out, b);
  or or_1 (out_3, and_1_out, and_2_out);
endmodule
