// Logisim project sub.circ as structural Verilog: 7 circuits, main circuit Additionneur
module main (
);

  Additionneur additionneur_1 ();  // open: a, b, cin, S, cout
endmodule

module Additionneur (
  input  a,
  input  b,
  input  cin,
  output S,
  output cout
);

  wire and_1_out, and_2_out, and_3_out, and_4_out, and_5_out, and_6_out, and_7_out, not_1_out, not_2_out,
       not_3_out, not_4_out, not_5_out, not_6_out;

  not not_1 (not_1_out, a);
  not not_2 (not_2_out, b);
  not not_3 (not_3_out, a);
  not not_4 (not_4_out, cin);
  not not_5 (not_5_out, b);
  not not_6 (not_6_out, cin);
  and and_1 (and_1_out, b, cin);
  and and_2 (and_2_out, a, cin);
  and and_3 (and_3_out, a, b);
  and and_4 (and_4_out, not_1_out, not_2_out, cin);
  and and_5 (and_5_out, not_3_out, b, not_4_out);
  and and_6 (and_6_out, a, not_5_out, not_6_out);
  and and_7 (and_7_out, a, b, cin);
  or or_1 (cout, and_1_out, and_2_out, and_3_out);
  or or_2 (S, and_4_out, and_5_out, and_6_out, and_7_out);
endmodule

module hg (
  input  in_1,
  input  [3:0] in_2,
  input  [3:0] in_3,
  output out_4
);

  wire additionneur_1_cout, additionneur_2_cout, additionneur_3_cout;
  wire [3:0] additionneur_1_s;

  Additionneur additionneur_1 (
    .a(in_2[0]), .b(in_3[0]), .cin(in_1), .S(additionneur_1_s[0]), .cout(additionneur_1_cout));
  Additionneur additionneur_2 (
    .a(in_2[1]), .b(in_3[1]), .cin(additionneur_1_cout), .S(additionneur_1_s[1]), .cout(additionneur_2_cout));
  Additionneur additionneur_3 (
    .a(in_2[2]), .b(in_3[2]), .cin(additionneur_2_cout), .S(additionneur_1_s[2]), .cout(additionneur_3_cout));
  Additionneur additionneur_4 (
    .a(in_2[3]), .b(in_3[3]), .cin(additionneur_3_cout), .S(additionneur_1_s[3]), .cout(out_4));
endmodule

module Soustracteur (
  input  in_1,
  input  [3:0] in_2,
  input  [3:0] in_3,
  output [3:0] out_4,
  output out_5
);

  wire additionneur_1_cout, additionneur_2_cout, additionneur_3_cout, not_1_out, not_2_out, not_3_out,
       not_4_out;

  not not_1 (not_1_out, in_3[0]);
  not not_2 (not_2_out, in_3[2]);
  not not_3 (not_3_out, in_3[3]);
  not not_4 (not_4_out, in_3[1]);
  Additionneur additionneur_1 (.a(in_2[0]), .b(not_1_out), .cin(in_1), .S(out_4[0]), .cout(additionneur_1_cout));
  Additionneur additionneur_2 (
    .a(in_2[1]), .b(not_4_out), .cin(additionneur_1_cout), .S(out_4[1]), .cout(additionneur_2_cout));
  Additionneur additionneur_3 (
    .a(in_2[2]), .b(not_2_out), .cin(additionneur_2_cout), .S(out_4[2]), .cout(additionneur_3_cout));
  Additionneur additionneur_4 (.a(in_2[3]), .b(not_3_out), .cin(additionneur_3_cout), .S(out_4[3]), .cout(out_5));
endmodule

module Comparateur (
  input  [3:0] in_1,
  input  [3:0] in_2
);

  wire not_1_out, not_2_out, not_3_out, not_4_out;

  not not_1 (not_1_out, in_2[3]);
  not not_2 (not_2_out, in_2[2]);
  not not_3 (not_3_out, in_2[1]);
  not not_4 (not_4_out, in_2[0]);
  // AND_Gate and_1 has open pins: in0=in_1[3], in4=not_1_out, out=open
  // AND_Gate and_2 has open pins: in0=in_1[2], in4=not_2_out, out=open
  // AND_Gate and_3 has open pins: in0=in_1[1], in4=not_3_out, out=open
  // AND_Gate and_4 has open pins: in0=in_1[0], in4=not_4_out, out=open
endmodule

module Multiplexer (
  input  a,
  input  e1,
  input  e2,
  output out_4
);

  wire and_1_out, and_2_out, not_1_out;

  not not_1 (not_1_out, a);
  and and_1 (and_1_out, not_1_out, e1);
  and and_2 (and_2_out, a, e2);
  or or_1 (out_4, and_1_out, and_2_out);
endmodule

module Multiplexer_x4 (
  input  a,
  input  b,
  input  e1,
  input  e2,
  input  e3,
  input  e4,
  output S
);

  wire and_1_out, and_2_out, and_3_out, and_4_out, not_1_out, not_2_out;

  not not_1 (not_1_out, b);
  not not_2 (not_2_out, a);
  and and_1 (and_1_out, not_2_out, not_1_out, e1);
  and and_2 (and_2_out, not_2_out, b, e2);
  and and_3 (and_3_out, not_1_out, a, e3);
  and and_4 (and_4_out, a, b, e4);
  or or_1 (S, and_1_out, and_2_out, and_3_out, and_4_out);
endmodule
